# Fritzing sketch cycle-through-numbers-in-seven-segment-led (saved by Fritzing 0.9.2b)
breadboards: 2

parts:
  7_Segment1 = 7 Segment Display
  Part1 = Arduino Uno (Rev3)
  U1 = 74HC595 [package="DIP16 [THT]"]
  R1 = Resistor [tolerance=±5% resistance=150 package=THT]
  R2 = Resistor [tolerance=±5% resistance=150 package=THT]
  R3 = Resistor [tolerance=±5% resistance=150 package=THT]
  R4 = Resistor [tolerance=±5% resistance=150 package=THT]
  R5 = Resistor [tolerance=±5% resistance=150 package=THT]
  R6 = Resistor [tolerance=±5% resistance=150 package=THT]
  R7 = Resistor [tolerance=±5% resistance=150 package=THT]
  R8 = Resistor [tolerance=±5% resistance=150 package=THT]

nets:
  N1: 7_Segment1.Segment_A#1, R7.Pin_0
  N2: 7_Segment1.Segment_F, R6.Pin_0
  N3: 7_Segment1.Segment_E, R3.Pin_0
  N4: 7_Segment1.Segment_D, R2.Pin_0
  N5: 7_Segment1.Segment_DP, R1.Pin_1
  N6: 7_Segment1.Segment_C, R4.Pin_1
  GND: 7_Segment1.common_cathode#8, Part1.GND, U1.GND, U1.OE
  N7: 7_Segment1.Segment_B, R8.Pin_0
  N8: 7_Segment1.Segment_A#10, R5.Pin_0
  N9: Part1.D8, U1.ST_CP
  N10: Part1.D11_PWM/MOSI, U1.DS
  N11: Part1.D12/MISO, U1.SH_CP
  5V: Part1.5V, U1.MR, U1.VCC
  N12: U1.Q1, R8.Pin_1
  N13: U1.Q2, R1.Pin_0
  N14: U1.Q3, R2.Pin_1
  N15: U1.Q4, R3.Pin_1
  N16: U1.Q5, R7.Pin_1
  N17: U1.Q6, R6.Pin_1
  N18: U1.Q7, R4.Pin_0
  N19: U1.Q0, R5.Pin_1

// code stored in the sketch: cycling-numbers-on-a-seven-segment-led.ino

